# Fritzing sketch FritzingSketch (saved by Fritzing 0.9.4)
breadboards: 1

parts:
  U1 = NodeMCU V3.0
  R1 = Photocell (LDR) [package=THT]
  S1 = Reed switch [package=THT]
  R1_2 = Resistor [tolerance=±5% resistance=10k package=THT]
  PIR1 = PIR sensor
  Part1 = DHT22 module

nets:
  N1: U1.D1, S1.pin_1
  GND: U1.GND#6, U1.GND#13, U1.GND#16, U1.GND#33, S1.pin_2, R1_2.Pin_1, PIR1.GND, Part1.GND
  N2: U1.D5, PIR1.SIG
  N3: U1.D6, Part1.DATA
  VIN: U1.Vin, R1.pin_0, PIR1.VDD, Part1.VCC
  N4: U1.A0, R1.pin_1, R1_2.Pin_0

custom parts:
  NodeMCU V3.0: ESP8266 based NodeMCU
